# Fritzing sketch Schematics (saved by Fritzing 0.9.3b)
breadboards: 1

parts:
  Part1 = Adafruit Bluefruit LE SPI Friend [part_number="Adafruit #2633"]
  Part2 = Arduino Uno (Rev3)
  U1 = L298 [package=multiwatt15]
  J1 = Piezo Speaker
  hc-sr1 = hc-sr04
  M1 = DC Motor
  M2 = DC Motor
  VCC1 = Battery block 9V

nets:
  N1: Part1.SCK, Part2.D13/SCK
  N2: Part1.MISO, Part2.D12/MISO
  N3: Part1.MOSI, Part2.D11_PWM/MOSI
  N4: Part1.CS, Part2.D8
  N5: Part1.IRQ, Part2.D7
  N6: Part1.RST, Part2.D4
  N7: Part2.A0, hc-sr1.Echo
  N8: Part2.A1, hc-sr1.Trig
  N9: Part2.A2, U1.IN1
  N10: Part2.D9_PWM, U1.ENA
  N11: Part2.D10_PWM/SS, U1.ENB
  GND: Part2.GND, U1.GND, J1.pin1, hc-sr1.GND, VCC1.-
  N12: Part2.D2, U1.IN2
  N13: Part2.D3_PWM, J1.pin2
  N14: Part2.D5_PWM, U1.IN3
  N15: Part2.D6_PWM, U1.IN4
  5V: Part2.5V, U1.VLS, hc-sr1.VCC
  N16: U1.OUT1, M2.pin_2
  N17: U1.OUT2, M2.pin_1
  N18: U1.VS, VCC1.+
  N19: U1.OUT3, M1.pin_2
  N20: U1.OUT4, M1.pin_1

custom parts:
  Adafruit Bluefruit LE SPI Friend: The Bluefruit LE SPI Friend makes it easy to add Bluetooth Low Energy connectivity to anything with 4 or 5 GPIO pins. With SPI, you don't have to worry about baud rates, flow control, or giving up a hardware UART port. Connect to your Arduino or other microcontroller using the common four-pin SPI interface (MISO, MOSI, SCK and CS) plus a 5th GPIO pin for interrupts (to let the Arduino know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
